# Fritzing sketch Pin_Configuration (saved by Fritzing 0.9.9b)
breadboards: 1

parts:
  MH-ET_Live_Minikit_for_ESP1 = MH-ET Live Minikit for ESP32
  Bauteil1 = Adafruit LIS3DH Triple-Axis Accelerometer [part_number="Adafruit #2809"]
  Bauteil2 = Adafruit VL530X Time of Flight Distance Sensor [part_number="Adafruit #3317"]

nets:
  GND: MH-ET_Live_Minikit_for_ESP1.GND, MH-ET_Live_Minikit_for_ESP1.TXD, Bauteil1.GND, Bauteil2.GND
  N1: MH-ET_Live_Minikit_for_ESP1.IO18, Bauteil2.SDA
  N2: MH-ET_Live_Minikit_for_ESP1.IO19, Bauteil2.SCL
  3.3V: MH-ET_Live_Minikit_for_ESP1.3.3V, Bauteil1.3.3V, Bauteil2.VCC
  N3: MH-ET_Live_Minikit_for_ESP1.IO27, Bauteil1.SDA
  N4: MH-ET_Live_Minikit_for_ESP1.IO25, Bauteil1.SCL

custom parts:
  MH-ET Live Minikit for ESP32: MH-ET Live Minikit for ESP32 ( http://mh.nodebb.com/topic/8/mh-et-live-minikit-for-esp32/2/) PCB footprint is invalid.
  Adafruit LIS3DH Triple-Axis Accelerometer: The LIS3DH is a very popular low power triple-axis accelerometer. It's low-cost, but has just about every 'extra' you'd want in an accelerometer: Three axis sensing, 10-bit precision ±2g/±4g/±8g/±16g selectable scaling Both I2C (2 possible addresses) and SPI interface options Interrupt output Multiple data rate options 1 Hz to 5Khz As low as 2uA current draw (just the chip itself, not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
  Adafruit VL530X Time of Flight Distance Sensor: The VL53L0X is a Time of Flight distance sensor like no other you've used! The sensor contains a very tiny invisible laser source, and a matching sensor. The VL53L0X can detect the "time of flight", or how long the light has taken to bounce back to the sensor. Since it uses a very narrow light source, it is good for determining distance of only the surface directly in front of it. Unlike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
